// Logisim project P0_L2_nonexist_2023.circ as structural Verilog: 2 circuits, main circuit main
module main (
  input  [7:0] in1,
  input  [7:0] in2,
  input  [7:0] in3,
  input  [7:0] in4,
  input  [7:0] in5,
  output [7:0] out_6
);

  wire has_n_1_out_7, has_n_2_out_7, has_n_3_out_7, has_n_4_out_7, has_n_5_out_7;
  wire [7:0] multiplexer_1_out, multiplexer_2_out, multiplexer_3_out, multiplexer_4_out;

  Multiplexer #(.width(8)) multiplexer_1 (
    .in0(8'h5), .in1(8'h6), .out(multiplexer_1_out), .sel(has_n_1_out_7));  // open: en
  has_n has_n_1 (.n(8'h5), .in_2(in1), .in_3(in2), .in_4(in3), .in_5(in4), .in_6(in5), .out_7(has_n_1_out_7));
  Multiplexer #(.width(8)) multiplexer_2 (
    .in0(8'h4), .in1(multiplexer_1_out), .out(multiplexer_2_out), .sel(has_n_2_out_7));  // open: en
  has_n has_n_2 (.n(8'h4), .in_2(in1), .in_3(in2), .in_4(in3), .in_5(in4), .in_6(in5), .out_7(has_n_2_out_7));
  Multiplexer #(.width(8)) multiplexer_3 (
    .in0(8'h3), .in1(multiplexer_2_out), .out(multiplexer_3_out), .sel(has_n_3_out_7));  // open: en
  has_n has_n_3 (.n(8'h3), .in_2(in1), .in_3(in2), .in_4(in3), .in_5(in4), .in_6(in5), .out_7(has_n_3_out_7));
  Multiplexer #(.width(8)) multiplexer_4 (
    .in0(8'h2), .in1(multiplexer_3_out), .out(multiplexer_4_out), .sel(has_n_4_out_7));  // open: en
  has_n has_n_4 (.n(8'h2), .in_2(in1), .in_3(in2), .in_4(in3), .in_5(in4), .in_6(in5), .out_7(has_n_4_out_7));
  has_n has_n_5 (.n(8'h1), .in_2(in1), .in_3(in2), .in_4(in3), .in_5(in4), .in_6(in5), .out_7(has_n_5_out_7));
  Multiplexer #(.width(8)) multiplexer_5 (
    .in0(8'h1), .in1(multiplexer_4_out), .out(out_6), .sel(has_n_5_out_7));  // open: en
endmodule

module has_n (
  input  [7:0] n,
  input  [7:0] in_2,
  input  [7:0] in_3,
  input  [7:0] in_4,
  input  [7:0] in_5,
  input  [7:0] in_6,
  output out_7
);

  wire comparator_1_eq, comparator_2_eq, comparator_3_eq, comparator_4_eq, comparator_5_eq;

  Comparator #(.mode("unsigned")) comparator_1 (.a(n), .b(in_2), .eq(comparator_1_eq));  // open: gt, lt
  Comparator #(.mode("unsigned")) comparator_2 (.a(n), .b(in_3), .eq(comparator_2_eq));  // open: gt, lt
  Comparator #(.mode("unsigned")) comparator_3 (.a(n), .b(in_4), .eq(comparator_3_eq));  // open: gt, lt
  Comparator #(.mode("unsigned")) comparator_4 (.a(n), .b(in_5), .eq(comparator_4_eq));  // open: gt, lt
  Comparator #(.mode("unsigned")) comparator_5 (.a(n), .b(in_6), .eq(comparator_5_eq));  // open: gt, lt
  or or_1 (out_7, comparator_1_eq, comparator_2_eq, comparator_3_eq, comparator_4_eq, comparator_5_eq);
endmodule
