// Logisim project fsm.circ as structural Verilog
module fsm (
  input  CLR,
  input  [1:0] In,
  output Z
);

  wire clock_1_out;
  wire [2:0] multiplexer_1_out, \状态存储_q , \状态转移_next_state ;

  \状态转移  \u_状态转移  (.state(\状态存储_q ), .\input (In), .next_state(\状态转移_next_state ));
  Multiplexer #(.width(3)) multiplexer_1 (
    .in0(\状态转移_next_state ), .in1(3'b000), .out(multiplexer_1_out), .sel(CLR));  // open: en
  Clock clock_1 (.out(clock_1_out));
  Register #(.width(3)) \u_状态存储  (.D(multiplexer_1_out), .Q(\状态存储_q ), .clk(clock_1_out));  // open: en, clr
  \输出逻辑  \u_输出逻辑  (.state(\状态存储_q ), .\input (In), .Z(Z));

  // Other names for the same wires on the sheet: 同步CLR = CLR
endmodule

module \状态转移  (
  input  [2:0] state,
  input  [1:0] \input ,
  output [2:0] next_state
);

  wire and_1_out, and_2_out, and_3_out, and_4_out, and_5_out, and_6_out, and_7_out, and_8_out, and_9_out,
       and_10_out, and_11_out, and_12_out, not_1_out, not_2_out, not_3_out, not_4_out, not_5_out, not_6_out,
       not_7_out, not_8_out, not_9_out, not_10_out, not_11_out, not_12_out, not_13_out, not_14_out,
       not_15_out, not_16_out, not_17_out, not_18_out, not_19_out, not_20_out, not_21_out, not_22_out,
       not_23_out, not_24_out, not_25_out, not_26_out, not_27_out, not_28_out;

  not not_1 (not_1_out, \input [0]);
  not not_2 (not_2_out, state[1]);
  not not_3 (not_3_out, state[0]);
  not not_4 (not_4_out, \input [0]);
  not not_5 (not_5_out, state[2]);
  not not_6 (not_6_out, state[1]);
  not not_7 (not_7_out, \input [1]);
  not not_8 (not_8_out, state[2]);
  not not_9 (not_9_out, state[1]);
  not not_10 (not_10_out, \input [0]);
  not not_11 (not_11_out, state[2]);
  not not_12 (not_12_out, state[0]);
  not not_13 (not_13_out, \input [1]);
  not not_14 (not_14_out, state[2]);
  not not_15 (not_15_out, state[0]);
  not not_16 (not_16_out, \input [0]);
  not not_17 (not_17_out, state[1]);
  not not_18 (not_18_out, state[0]);
  not not_19 (not_19_out, \input [0]);
  not not_20 (not_20_out, state[1]);
  not not_21 (not_21_out, state[0]);
  not not_22 (not_22_out, \input [1]);
  not not_23 (not_23_out, state[2]);
  not not_24 (not_24_out, \input [0]);
  not not_25 (not_25_out, state[2]);
  not not_26 (not_26_out, \input [0]);
  not not_27 (not_27_out, \input [1]);
  not not_28 (not_28_out, \input [1]);
  and and_1 (and_1_out, state[1], state[0], not_1_out);
  and and_2 (and_2_out, state[2], not_2_out, not_3_out, not_4_out);
  and and_3 (and_3_out, not_5_out, not_6_out, state[0], not_7_out);
  and and_4 (and_4_out, not_8_out, not_9_out, state[0], not_10_out);
  and and_5 (and_5_out, not_11_out, state[1], not_12_out, not_13_out);
  and and_6 (and_6_out, not_14_out, state[1], not_15_out, not_16_out);
  and and_7 (and_7_out, state[2], not_17_out, not_18_out, not_19_out);
  and and_8 (and_8_out, not_20_out, not_21_out, not_22_out, \input [0]);
  and and_9 (and_9_out, not_23_out, state[0], not_24_out);
  and and_10 (and_10_out, not_25_out, state[1], not_26_out);
  and and_11 (and_11_out, state[1], state[0], not_27_out);
  and and_12 (and_12_out, state[2], not_28_out, \input [0]);
  or or_1 (next_state[2], and_1_out, and_2_out);
  or or_2 (next_state[1], and_3_out, and_4_out, and_5_out, and_6_out, and_7_out);
  or or_3 (next_state[0], and_8_out, and_9_out, and_10_out, and_11_out, and_12_out);
endmodule

module \输出逻辑  (
  input  [2:0] state,
  input  [1:0] \input ,
  output Z
);

  wire and_1_out, and_2_out, not_1_out, not_2_out, not_3_out, not_4_out, not_5_out;

  not not_1 (not_1_out, state[2]);
  not not_2 (not_2_out, \input [0]);
  not not_3 (not_3_out, state[1]);
  not not_4 (not_4_out, state[0]);
  not not_5 (not_5_out, \input [0]);
  and and_1 (and_1_out, not_1_out, state[1], state[0], not_2_out);
  and and_2 (and_2_out, state[2], not_3_out, not_4_out, not_5_out);
  or or_1 (Z, and_1_out, and_2_out);
endmodule
