// Logisim project navigation(encode via one-hot).circ as structural Verilog
module navigation (
  input  [1:0] dir,
  input  clk,
  input  reset,
  output out_4,
  output hit
);

  wire counter_1_q, \状态转移_1_hit ;
  wire [4:0] multiplexer_1_out, state_q, \状态转移_1_next_state ;

  \状态转移  \u_状态转移_1  (.state(multiplexer_1_out), .In(dir), .next_state(\状态转移_1_next_state ), .hit(\状态转移_1_hit ));
  // Probe on state_q
  Register #(.width(5)) state (.D(\状态转移_1_next_state ), .Q(state_q), .clk(clk), .clr(reset));  // open: en
  Register #(.width(1)) u_hit (.D(\状态转移_1_hit ), .Q(hit), .clk(clk), .clr(reset));  // open: en
  Counter #(.width(1), .max('h1), .ongoal("stay")) counter_1 (
    .Q(counter_1_q), .clk(clk), .clr(reset));  // open: load, D, count, carry
  Multiplexer #(.width(5)) multiplexer_1 (
    .in0(5'b00001), .in1(state_q), .out(multiplexer_1_out), .sel(counter_1_q));  // open: en
  Comparator #(.width(5), .mode("unsigned")) comparator_1 (
    .a(5'b10000), .b(multiplexer_1_out), .eq(out_4));  // open: gt, lt
endmodule

module \状态转移  (
  input  [4:0] state,
  input  [1:0] In,
  output [4:0] next_state,
  output hit
);

  wire and_1_out, and_2_out, and_3_out, and_4_out, and_5_out, and_6_out, and_7_out, and_8_out, and_9_out,
       and_10_out, and_11_out, and_12_out, and_13_out, and_14_out, and_15_out, and_16_out, \东 , \北 , \南 , \西 ;

  Decoder #(.select(2)) decoder_1 (.out0(\北 ), .out1(\东 ), .out2(\南 ), .out3(\西 ), .sel(In));  // open: en
  and and_1 (and_1_out, state[1], \南 );
  and and_2 (and_2_out, state[0], \西 );
  and and_3 (and_3_out, state[0], \南 );
  and and_4 (and_4_out, state[0], \东 );
  and and_5 (and_5_out, state[0], \北 );
  and and_6 (and_6_out, state[2], \西 );
  and and_7 (and_7_out, state[3], \南 );
  and and_8 (and_8_out, state[1], \西 );
  and and_9 (and_9_out, state[2], \南 );
  and and_10 (and_10_out, state[2], \东 );
  and and_11 (and_11_out, state[1], \东 );
  or or_1 (next_state[0], and_1_out, and_2_out, state[4], and_3_out, and_4_out);
  or or_2 (next_state[1], and_5_out, and_6_out, and_7_out, and_8_out);
  or or_3 (next_state[2], and_9_out, and_10_out, and_11_out);
  and and_12 (and_12_out, state[3], \西 );
  and and_13 (and_13_out, state[1], \北 );
  or or_4 (hit, and_14_out, and_12_out, and_2_out, and_3_out, and_4_out, and_8_out, and_9_out, and_10_out);
  and and_14 (and_14_out, state[3], \北 );
  and and_15 (and_15_out, state[3], \东 );
  and and_16 (and_16_out, state[2], \北 );
  or or_5 (next_state[3], and_14_out, and_12_out, and_13_out);
  or or_6 (next_state[4], and_15_out, and_16_out);

  // Other names for the same wires on the sheet: next_A = next_state[0]; next_X = next_state[1];
  //   next_Y = next_state[2]; next_Z = next_state[3]; next_B = next_state[4]; A = state[0]; X = state[1];
  //   Y = state[2]; Z = state[3]; B = state[4]
endmodule
