// Logisim project navigation.circ as structural Verilog
module navigation (
  input  [1:0] dir,
  input  clk,
  input  reset,
  output arrive,
  output hit
);

  wire [3:0] \状态转移_1_next_withhit ;
  wire [3:1] \状态存储_next_hit_q ;

  \状态转移  \u_状态转移_1  (.state(\状态存储_next_hit_q ), .dir(dir), .next_withHit(\状态转移_1_next_withhit ));
  // Probe on \状态存储_next_hit_q 
  Register #(.width(4)) \u_状态存储_next_hit  (
    .D(\状态转移_1_next_withhit ), .Q({\状态存储_next_hit_q , hit}), .clk(clk), .clr(reset));  // open: en
  Comparator #(.width(3), .mode("unsigned")) comparator_1 (
    .a(3'b100), .b(\状态存储_next_hit_q ), .eq(arrive));  // open: gt, lt
endmodule

module \状态转移  (
  input  [2:0] state,
  input  [1:0] dir,
  output [3:0] next_withHit
);

  wire and_1_out, and_2_out, and_3_out, and_4_out, and_5_out, and_6_out, and_7_out, and_8_out, and_9_out,
       and_10_out, and_11_out, and_12_out, and_13_out, and_14_out, and_15_out, and_16_out, not_1_out,
       not_2_out, not_3_out, not_4_out, not_5_out, not_6_out, not_7_out, not_8_out, not_9_out, not_10_out,
       not_11_out, not_12_out, not_13_out, not_14_out, not_15_out, not_16_out, not_17_out, not_18_out,
       not_19_out, not_20_out, not_21_out, not_22_out, not_23_out, not_24_out, not_25_out, not_26_out,
       not_27_out, not_28_out, not_29_out, not_30_out, not_31_out, not_32_out, not_33_out, not_34_out,
       not_35_out, not_36_out, not_37_out, not_38_out, not_39_out, not_40_out;

  not not_1 (not_1_out, state[2]);
  not not_2 (not_2_out, state[0]);
  not not_3 (not_3_out, dir[1]);
  not not_4 (not_4_out, dir[0]);
  not not_5 (not_5_out, state[2]);
  not not_6 (not_6_out, dir[1]);
  not not_7 (not_7_out, state[2]);
  not not_8 (not_8_out, state[1]);
  not not_9 (not_9_out, dir[1]);
  not not_10 (not_10_out, state[2]);
  not not_11 (not_11_out, dir[1]);
  not not_12 (not_12_out, dir[0]);
  not not_13 (not_13_out, state[2]);
  not not_14 (not_14_out, state[0]);
  not not_15 (not_15_out, dir[1]);
  not not_16 (not_16_out, state[2]);
  not not_17 (not_17_out, state[0]);
  not not_18 (not_18_out, dir[0]);
  not not_19 (not_19_out, state[2]);
  not not_20 (not_20_out, state[2]);
  not not_21 (not_21_out, state[1]);
  not not_22 (not_22_out, dir[1]);
  not not_23 (not_23_out, dir[0]);
  not not_24 (not_24_out, state[2]);
  not not_25 (not_25_out, state[2]);
  not not_26 (not_26_out, state[2]);
  not not_27 (not_27_out, dir[0]);
  not not_28 (not_28_out, state[2]);
  not not_29 (not_29_out, state[0]);
  not not_30 (not_30_out, dir[1]);
  not not_31 (not_31_out, state[2]);
  not not_32 (not_32_out, state[1]);
  not not_33 (not_33_out, state[0]);
  not not_34 (not_34_out, state[2]);
  not not_35 (not_35_out, state[0]);
  not not_36 (not_36_out, dir[0]);
  not not_37 (not_37_out, state[2]);
  not not_38 (not_38_out, state[2]);
  not not_39 (not_39_out, dir[1]);
  not not_40 (not_40_out, dir[0]);
  and and_1 (and_1_out, not_1_out, state[1], not_2_out, not_3_out, not_4_out);
  and and_2 (and_2_out, not_5_out, state[1], state[0], not_6_out, dir[0]);
  and and_3 (and_3_out, not_7_out, not_8_out, state[0], not_9_out);
  and and_4 (and_4_out, not_10_out, state[0], not_11_out, not_12_out);
  and and_5 (and_5_out, not_13_out, state[1], not_14_out, not_15_out, dir[0]);
  and and_6 (and_6_out, not_16_out, state[1], not_17_out, dir[1], not_18_out);
  and and_7 (and_7_out, not_19_out, state[1], state[0], dir[1], dir[0]);
  and and_8 (and_8_out, not_20_out, not_21_out, not_22_out, not_23_out);
  and and_9 (and_9_out, not_24_out, state[0], dir[1], dir[0]);
  and and_10 (and_10_out, not_25_out, state[1], dir[1], dir[0]);
  and and_11 (and_11_out, not_26_out, state[1], state[0], not_27_out);
  and and_12 (and_12_out, not_28_out, not_29_out, not_30_out, dir[0]);
  and and_13 (and_13_out, not_31_out, not_32_out, not_33_out, dir[1]);
  and and_14 (and_14_out, not_34_out, not_35_out, dir[1], not_36_out);
  and and_15 (and_15_out, not_37_out, state[0], dir[1], dir[0]);
  and and_16 (and_16_out, not_38_out, state[1], state[0], not_39_out, not_40_out);
  or or_1 (next_withHit[3], and_1_out, and_2_out);
  or or_2 (next_withHit[2], and_3_out, and_4_out, and_5_out, and_6_out, and_7_out);
  or or_3 (next_withHit[1], and_8_out, and_9_out, and_10_out, and_11_out);
  or or_4 (next_withHit[0], and_12_out, and_13_out, and_14_out, and_15_out, and_16_out);
endmodule
