// Logisim project CRC.circ as structural Verilog
module mod2_div_4bit (
  input  [3:0] \被除数 ,
  input  [3:0] \除数 ,
  output [2:0] \余数 ,
  output \商 
);

  wire comparator_1_eq;
  wire [2:0] xor_1_out;

  // Probe on \被除数 [2:0]
  // Probe on \被除数 [3]
  assign xor_1_out = \被除数 [2:0] ^ \除数 [2:0];  // XOR_Gate xor_1, 3 bits wide
  Comparator #(.width(1), .mode("unsigned")) comparator_1 (
    .a(\被除数 [3]), .b(1'b1), .eq(comparator_1_eq));  // open: gt, lt
  Multiplexer #(.width(3)) multiplexer_1 (
    .in0(\被除数 [2:0]), .in1(xor_1_out), .out(\余数 ), .sel(comparator_1_eq));  // open: en
  Multiplexer multiplexer_2 (.in0(1'b0), .in1(1'b1), .out(\商 ), .sel(comparator_1_eq));  // open: en
endmodule

module CRC (
  input  [7:0] \原数据帧 ,
  input  [3:0] \除数 ,
  output [10:0] \_8位原帧_3位校验码 
);

  wire [2:0] \mod2_div_4bit_1_余数 , \mod2_div_4bit_2_余数 , \mod2_div_4bit_3_余数 , \mod2_div_4bit_4_余数 ,
       \mod2_div_4bit_5_余数 , \mod2_div_4bit_6_余数 ;
  wire [3:1] \mod2_div_4bit_7_余数 ;
  wire [10:0] bit_extender_1_out, shifter_1_out;

  assign bit_extender_1_out = {{3{1'b0}}, \原数据帧 };  // Bit_Extender bit_extender_1
  Shifter #(.width(11)) shifter_1 (.in(bit_extender_1_out), .\dist (4'b0011), .out(shifter_1_out));
  // Probe on shifter_1_out
  mod2_div_4bit mod2_div_4bit_1 (.\被除数 (shifter_1_out[10:7]), .\除数 (\除数 ), .\余数 (\mod2_div_4bit_1_余数 ));  // open: 商
  mod2_div_4bit mod2_div_4bit_2 (
    .\被除数 ({\mod2_div_4bit_6_余数 , shifter_1_out[5]}), .\除数 (\除数 ), .\余数 (\mod2_div_4bit_2_余数 ));  // open: 商
  mod2_div_4bit mod2_div_4bit_3 (
    .\被除数 ({\mod2_div_4bit_7_余数 , shifter_1_out[2]}), .\除数 (\除数 ), .\余数 (\mod2_div_4bit_3_余数 ));  // open: 商
  mod2_div_4bit mod2_div_4bit_4 (
    .\被除数 ({\mod2_div_4bit_2_余数 , shifter_1_out[4]}), .\除数 (\除数 ), .\余数 (\mod2_div_4bit_4_余数 ));  // open: 商
  mod2_div_4bit mod2_div_4bit_5 (
    .\被除数 ({\mod2_div_4bit_3_余数 , shifter_1_out[1]}), .\除数 (\除数 ), .\余数 (\mod2_div_4bit_5_余数 ));  // open: 商
  mod2_div_4bit mod2_div_4bit_6 (
    .\被除数 ({\mod2_div_4bit_1_余数 , shifter_1_out[6]}), .\除数 (\除数 ), .\余数 (\mod2_div_4bit_6_余数 ));  // open: 商
  mod2_div_4bit mod2_div_4bit_7 (
    .\被除数 ({\mod2_div_4bit_4_余数 , shifter_1_out[3]}), .\除数 (\除数 ), .\余数 (\mod2_div_4bit_7_余数 ));  // open: 商
  mod2_div_4bit mod2_div_4bit_8 (
    .\被除数 ({\mod2_div_4bit_5_余数 , shifter_1_out[0]}), .\除数 (\除数 ), .\余数 (\_8位原帧_3位校验码 [2:0]));  // open: 商

  assign \_8位原帧_3位校验码 [10:3] = \原数据帧 ;
endmodule
