// Logisim project ftoi.circ as structural Verilog
module ftoi (
  input  [15:0] in_1,
  output [31:0] \int 
);

  wire comparator_1_eq, comparator_2_lt, comparator_3_eq, comparator_4_eq;
  wire [4:0] multiplexer_2_out, subtractor_1_out, subtractor_2_out;
  wire [31:0] adder_1_out, adder_2_out, adder_3_out, adder_4_out, adder_5_out, adder_6_out, adder_7_out,
       adder_8_out, adder_9_out, adder_10_out, multiplexer_1_out, multiplexer_3_out, multiplexer_4_out,
       multiplexer_5_out, multiplexer_6_out, multiplexer_7_out, multiplexer_8_out, multiplexer_9_out,
       multiplexer_10_out, multiplexer_11_out, multiplexer_12_out, multiplexer_13_out, multiplexer_14_out,
       multiplexer_15_out, multiplexer_16_out, multiplexer_17_out, multiplexer_18_out, multiplexer_19_out,
       multiplexer_20_out, multiplexer_21_out, multiplexer_22_out, multiplexer_23_out, multiplexer_24_out,
       multiplexer_25_out, negator_1_out, shifter_1_out, shifter_2_out, shifter_3_out, shifter_4_out,
       shifter_5_out, shifter_6_out, shifter_7_out, shifter_8_out, shifter_9_out, shifter_10_out,
       shifter_11_out, shifter_12_out, shifter_13_out, shifter_14_out, shifter_15_out, shifter_16_out,
       shifter_17_out, shifter_18_out, shifter_19_out, shifter_20_out, shifter_21_out, shifter_22_out,
       shifter_23_out, shifter_24_out, shifter_25_out, shifter_26_out, shifter_27_out, shifter_28_out,
       shifter_29_out, shifter_30_out, shifter_31_out, shifter_32_out;

  Comparator #(.width(5)) comparator_1 (.a(in_1[14:10]), .b({5{1'b0}}), .eq(comparator_1_eq));  // open: gt, lt
  Comparator #(.width(5), .mode("unsigned")) comparator_2 (
    .a(in_1[14:10]), .b(5'b01111), .lt(comparator_2_lt));  // open: gt, eq
  Multiplexer #(.width(32)) multiplexer_1 (
    .in0(32'h1), .in1({32{1'b0}}), .out(multiplexer_1_out), .sel(comparator_1_eq));  // open: en
  Subtractor #(.width(5)) subtractor_1 (.a(in_1[14:10]), .b(5'b01111), .out(subtractor_1_out));  // open: bin, bout
  Subtractor #(.width(5)) subtractor_2 (.a(5'b01111), .b(in_1[14:10]), .out(subtractor_2_out));  // open: bin, bout
  Multiplexer #(.width(5)) multiplexer_2 (
    .in0(subtractor_1_out), .in1(subtractor_2_out), .out(multiplexer_2_out), .sel(comparator_2_lt));  // open: en
  Shifter #(.width(32)) shifter_1 (.in(multiplexer_1_out), .\dist (multiplexer_2_out), .out(shifter_1_out));
  Shifter #(.width(32), .shift("lr")) shifter_2 (
    .in(multiplexer_1_out), .\dist (multiplexer_2_out), .out(shifter_2_out));
  Shifter #(.width(32)) shifter_3 (.in(32'h1), .\dist (multiplexer_2_out), .out(shifter_3_out));
  Shifter #(.width(32), .shift("lr")) shifter_4 (.in(32'h1), .\dist (multiplexer_2_out), .out(shifter_4_out));
  Shifter #(.width(32)) shifter_5 (.in(32'h1), .\dist (multiplexer_2_out), .out(shifter_5_out));
  Shifter #(.width(32), .shift("lr")) shifter_6 (.in(32'h1), .\dist (multiplexer_2_out), .out(shifter_6_out));
  Shifter #(.width(32)) shifter_7 (.in(32'h1), .\dist (multiplexer_2_out), .out(shifter_7_out));
  Shifter #(.width(32), .shift("lr")) shifter_8 (.in(32'h1), .\dist (multiplexer_2_out), .out(shifter_8_out));
  Shifter #(.width(32)) shifter_9 (.in(32'h1), .\dist (multiplexer_2_out), .out(shifter_9_out));
  Shifter #(.width(32), .shift("lr")) shifter_10 (.in(32'h1), .\dist (multiplexer_2_out), .out(shifter_10_out));
  Shifter #(.width(32)) shifter_11 (.in(32'h1), .\dist (multiplexer_2_out), .out(shifter_11_out));
  Shifter #(.width(32), .shift("lr")) shifter_12 (.in(32'h1), .\dist (multiplexer_2_out), .out(shifter_12_out));
  Shifter #(.width(32)) shifter_13 (.in(32'h1), .\dist (multiplexer_2_out), .out(shifter_13_out));
  Shifter #(.width(32), .shift("lr")) shifter_14 (.in(32'h1), .\dist (multiplexer_2_out), .out(shifter_14_out));
  Shifter #(.width(32)) shifter_15 (.in(32'h1), .\dist (multiplexer_2_out), .out(shifter_15_out));
  Shifter #(.width(32), .shift("lr")) shifter_16 (.in(32'h1), .\dist (multiplexer_2_out), .out(shifter_16_out));
  Shifter #(.width(32)) shifter_17 (.in(32'h1), .\dist (multiplexer_2_out), .out(shifter_17_out));
  Shifter #(.width(32), .shift("lr")) shifter_18 (.in(32'h1), .\dist (multiplexer_2_out), .out(shifter_18_out));
  Shifter #(.width(32)) shifter_19 (.in(32'h1), .\dist (multiplexer_2_out), .out(shifter_19_out));
  Shifter #(.width(32), .shift("lr")) shifter_20 (.in(32'h1), .\dist (multiplexer_2_out), .out(shifter_20_out));
  Shifter #(.width(32)) shifter_21 (.in(32'h1), .\dist (multiplexer_2_out), .out(shifter_21_out));
  Shifter #(.width(32), .shift("lr")) shifter_22 (.in(32'h1), .\dist (multiplexer_2_out), .out(shifter_22_out));
  Multiplexer #(.width(32)) multiplexer_3 (
    .in0(shifter_1_out), .in1(shifter_2_out), .out(multiplexer_3_out), .sel(comparator_2_lt));  // open: en
  Multiplexer #(.width(32)) multiplexer_4 (
    .in0(shifter_3_out), .in1(shifter_4_out), .out(multiplexer_4_out), .sel(comparator_2_lt));  // open: en
  Multiplexer #(.width(32)) multiplexer_5 (
    .in0(shifter_5_out), .in1(shifter_6_out), .out(multiplexer_5_out), .sel(comparator_2_lt));  // open: en
  Multiplexer #(.width(32)) multiplexer_6 (
    .in0(shifter_7_out), .in1(shifter_8_out), .out(multiplexer_6_out), .sel(comparator_2_lt));  // open: en
  Multiplexer #(.width(32)) multiplexer_7 (
    .in0(shifter_9_out), .in1(shifter_10_out), .out(multiplexer_7_out), .sel(comparator_2_lt));  // open: en
  Multiplexer #(.width(32)) multiplexer_8 (
    .in0(shifter_11_out), .in1(shifter_12_out), .out(multiplexer_8_out), .sel(comparator_2_lt));  // open: en
  Multiplexer #(.width(32)) multiplexer_9 (
    .in0(shifter_13_out), .in1(shifter_14_out), .out(multiplexer_9_out), .sel(comparator_2_lt));  // open: en
  Multiplexer #(.width(32)) multiplexer_10 (
    .in0(shifter_15_out), .in1(shifter_16_out), .out(multiplexer_10_out), .sel(comparator_2_lt));  // open: en
  Multiplexer #(.width(32)) multiplexer_11 (
    .in0(shifter_17_out), .in1(shifter_18_out), .out(multiplexer_11_out), .sel(comparator_2_lt));  // open: en
  Multiplexer #(.width(32)) multiplexer_12 (
    .in0(shifter_19_out), .in1(shifter_20_out), .out(multiplexer_12_out), .sel(comparator_2_lt));  // open: en
  Multiplexer #(.width(32)) multiplexer_13 (
    .in0(shifter_21_out), .in1(shifter_22_out), .out(multiplexer_13_out), .sel(comparator_2_lt));  // open: en
  Shifter #(.width(32), .shift("lr")) shifter_23 (.in(multiplexer_4_out), .\dist (5'b00001), .out(shifter_23_out));
  Shifter #(.width(32), .shift("lr")) shifter_24 (.in(multiplexer_5_out), .\dist (5'b00010), .out(shifter_24_out));
  Shifter #(.width(32), .shift("lr")) shifter_25 (.in(multiplexer_6_out), .\dist (5'b00011), .out(shifter_25_out));
  Shifter #(.width(32), .shift("lr")) shifter_26 (.in(multiplexer_7_out), .\dist (5'b00100), .out(shifter_26_out));
  Shifter #(.width(32), .shift("lr")) shifter_27 (.in(multiplexer_8_out), .\dist (5'b00101), .out(shifter_27_out));
  Shifter #(.width(32), .shift("lr")) shifter_28 (.in(multiplexer_9_out), .\dist (5'b00110), .out(shifter_28_out));
  Shifter #(.width(32), .shift("lr")) shifter_29 (.in(multiplexer_10_out), .\dist (5'b00111), .out(shifter_29_out));
  Shifter #(.width(32), .shift("lr")) shifter_30 (.in(multiplexer_11_out), .\dist (5'b01000), .out(shifter_30_out));
  Shifter #(.width(32), .shift("lr")) shifter_31 (.in(multiplexer_12_out), .\dist (5'b01001), .out(shifter_31_out));
  Shifter #(.width(32), .shift("lr")) shifter_32 (.in(multiplexer_13_out), .\dist (5'b01010), .out(shifter_32_out));
  Multiplexer #(.width(32)) multiplexer_14 (
    .in0({32{1'b0}}), .in1(shifter_23_out), .out(multiplexer_14_out), .sel(in_1[9]));  // open: en
  Multiplexer #(.width(32)) multiplexer_15 (
    .in0({32{1'b0}}), .in1(shifter_24_out), .out(multiplexer_15_out), .sel(in_1[8]));  // open: en
  Multiplexer #(.width(32)) multiplexer_16 (
    .in0({32{1'b0}}), .in1(shifter_25_out), .out(multiplexer_16_out), .sel(in_1[7]));  // open: en
  Multiplexer #(.width(32)) multiplexer_17 (
    .in0({32{1'b0}}), .in1(shifter_26_out), .out(multiplexer_17_out), .sel(in_1[6]));  // open: en
  Multiplexer #(.width(32)) multiplexer_18 (
    .in0({32{1'b0}}), .in1(shifter_27_out), .out(multiplexer_18_out), .sel(in_1[5]));  // open: en
  Multiplexer #(.width(32)) multiplexer_19 (
    .in0({32{1'b0}}), .in1(shifter_28_out), .out(multiplexer_19_out), .sel(in_1[4]));  // open: en
  Multiplexer #(.width(32)) multiplexer_20 (
    .in0({32{1'b0}}), .in1(shifter_29_out), .out(multiplexer_20_out), .sel(in_1[3]));  // open: en
  Multiplexer #(.width(32)) multiplexer_21 (
    .in0({32{1'b0}}), .in1(shifter_30_out), .out(multiplexer_21_out), .sel(in_1[2]));  // open: en
  Multiplexer #(.width(32)) multiplexer_22 (
    .in0({32{1'b0}}), .in1(shifter_31_out), .out(multiplexer_22_out), .sel(in_1[1]));  // open: en
  Multiplexer #(.width(32)) multiplexer_23 (
    .in0({32{1'b0}}), .in1(shifter_32_out), .out(multiplexer_23_out), .sel(in_1[0]));  // open: en
  Multiplexer #(.width(32)) multiplexer_24 (
    .in0(adder_10_out), .in1({32{1'b0}}), .out(multiplexer_24_out), .sel(comparator_3_eq));  // open: en
  Comparator #(.width(5), .mode("unsigned")) comparator_3 (
    .a(in_1[14:10]), .b({5{1'b1}}), .eq(comparator_3_eq));  // open: gt, lt
  Comparator #(.width(5), .mode("unsigned")) comparator_4 (
    .a(in_1[14:10]), .b({5{1'b0}}), .eq(comparator_4_eq));  // open: gt, lt
  Adder #(.width(32)) adder_1 (.a(multiplexer_14_out), .b(multiplexer_15_out), .out(adder_1_out));  // open: cin, cout
  Adder #(.width(32)) adder_2 (.a(multiplexer_16_out), .b(multiplexer_17_out), .out(adder_2_out));  // open: cin, cout
  Adder #(.width(32)) adder_3 (.a(multiplexer_18_out), .b(multiplexer_19_out), .out(adder_3_out));  // open: cin, cout
  Adder #(.width(32)) adder_4 (.a(multiplexer_20_out), .b(multiplexer_21_out), .out(adder_4_out));  // open: cin, cout
  Adder #(.width(32)) adder_5 (.a(multiplexer_22_out), .b(multiplexer_23_out), .out(adder_5_out));  // open: cin, cout
  Multiplexer #(.width(32)) multiplexer_25 (
    .in0(multiplexer_24_out), .in1({32{1'b0}}), .out(multiplexer_25_out), .sel(comparator_4_eq));  // open: en
  Adder #(.width(32)) adder_6 (.a(multiplexer_3_out), .b(adder_1_out), .out(adder_6_out));  // open: cin, cout
  Adder #(.width(32)) adder_7 (.a(adder_2_out), .b(adder_3_out), .out(adder_7_out));  // open: cin, cout
  Adder #(.width(32)) adder_8 (.a(adder_4_out), .b(adder_5_out), .out(adder_8_out));  // open: cin, cout
  Multiplexer #(.width(32)) multiplexer_26 (
    .in0(multiplexer_25_out), .in1(negator_1_out), .out(\int ), .sel(in_1[15]));  // open: en
  Negator #(.width(32)) negator_1 (.in(multiplexer_25_out), .out(negator_1_out));
  Adder #(.width(32)) adder_9 (.a(adder_7_out), .b(adder_8_out), .out(adder_9_out));  // open: cin, cout
  Adder #(.width(32)) adder_10 (.a(adder_6_out), .b(adder_9_out), .out(adder_10_out));  // open: cin, cout

  // Other names for the same wires on the sheet: frac[9:0] = in_1[9:0]; minus_10 = in_1[0]; minus_9 = in_1[1];
  //   minus_8 = in_1[2]; minus_7 = in_1[3]; minus_6 = in_1[4]; minus_5 = in_1[5]; minus_4 = in_1[6];
  //   minus_3 = in_1[7]; minus_2 = in_1[8]; minus_1 = in_1[9]; Exp[4:0] = in_1[14:10]; sign = in_1[15]
endmodule
