// Logisim project P0_L0_sinking_2023.circ as structural Verilog: 2 circuits, main circuit main
module main (
  input  [7:0] \input ,
  input  clk,
  input  reset,
  output [7:0] \output 
);

  wire comparator_1_eq;
  wire [7:0] multiplexer_1_out, \状态转移_next_state ;

  \状态转移  \u_状态转移  (.state(\output ), .next_state(\状态转移_next_state ));
  Multiplexer #(.width(8)) multiplexer_1 (
    .in0(\input ), .in1(\状态转移_next_state ), .out(multiplexer_1_out), .sel(comparator_1_eq));  // open: en
  Comparator #(.mode("unsigned")) comparator_1 (.a(\input ), .b({8{1'b0}}), .eq(comparator_1_eq));  // open: gt, lt
  Register register_1 (.D(multiplexer_1_out), .Q(\output ), .clk(clk), .clr(reset));  // open: en
endmodule

module \状态转移  (
  input  [7:0] state,
  output [7:0] next_state
);

  wire comparator_1_eq;
  wire [2:0] bitfinder_1_index;
  wire [7:0] multiplexer_1_out, or_1_out, shifter_1_out;

  // Probe on shifter_1_out
  Shifter #(.shift("lr")) shifter_1 (.in(state), .\dist (3'b001), .out(shifter_1_out));
  // Probe on bitfinder_1_index
  BitFinder #(.\type ("low0")) bitfinder_1 (.in(state), .index(bitfinder_1_index));  // open: found
  Comparator #(.mode("unsigned")) comparator_1 (.a(state), .b({8{1'b1}}), .eq(comparator_1_eq));  // open: gt, lt
  Multiplexer #(.select(3), .width(8)) multiplexer_1 (
    .in0({8{1'b0}}), .in1(8'h1), .in2(8'h3), .in3(8'h7), .in4(8'hf), .in5(8'h1f), .in6(8'h3f), .in7(8'h7f),
    .out(multiplexer_1_out), .sel(bitfinder_1_index));  // open: en
  assign or_1_out = shifter_1_out | multiplexer_1_out;  // OR_Gate or_1, 8 bits wide
  Multiplexer #(.width(8)) multiplexer_2 (
    .in0(or_1_out), .in1(state), .out(next_state), .sel(comparator_1_eq));  // open: en
endmodule
