// Logisim project P0_L1_gray_2023.circ as structural Verilog: 1 circuit, main circuit main
// 2
module main (
  input  [7:0] in_1,
  output [7:0] out_2
);

  wire comparator_1_eq;
  wire [2:0] adder_1_out, bitfinder_1_index, multiplexer_1_out;
  wire [3:0] bitadder_1_out;
  wire [7:0] shifter_1_out, xor_1_out;

  BitFinder bitfinder_1 (.in(in_1), .index(bitfinder_1_index));  // open: found
  BitAdder bitadder_1 (.in0(in_1), .out(bitadder_1_out));
  Comparator #(.mode("unsigned")) comparator_1 (.a(in_1), .b(8'h80), .eq(comparator_1_eq));  // open: gt, lt
  Adder #(.width(3)) adder_1 (.a(3'b001), .b(bitfinder_1_index), .out(adder_1_out));  // open: cin, cout
  Multiplexer #(.width(3)) multiplexer_1 (
    .in0(3'b000), .in1(adder_1_out), .out(multiplexer_1_out), .sel(bitadder_1_out[0]));  // open: en
  Shifter shifter_1 (.in(8'h1), .\dist (multiplexer_1_out), .out(shifter_1_out));
  assign xor_1_out = in_1 ^ shifter_1_out;  // XOR_Gate xor_1, 8 bits wide
  Multiplexer #(.width(8)) multiplexer_2 (
    .in0(xor_1_out), .in1({8{1'b0}}), .out(out_2), .sel(comparator_1_eq));  // open: en
endmodule
