// Logisim project P0_L1_mips.circ as structural Verilog
module mips (
  input  [1:0] in,
  input  clk,
  input  reset,
  output [1:0] \output 
);

  wire comparator_1_eq, comparator_2_eq;
  wire [1:0] multiplexer_2_out;
  wire [3:0] multiplexer_1_out;
  wire [11:0] bit_extender_1_out, or_1_out, register_1_q, shifter_1_out;

  Shifter #(.width(12)) shifter_1 (.in(register_1_q), .\dist (4'b0100), .out(shifter_1_out));
  assign bit_extender_1_out = {{8{1'b0}}, multiplexer_1_out};  // Bit_Extender bit_extender_1
  Multiplexer #(.select(2), .width(4)) multiplexer_1 (
    .in0(4'b0010), .in1(4'b0100), .in2(4'b1000), .in3(4'b1111), .out(multiplexer_1_out), .sel(in));  // open: en
  // Probe on or_1_out
  assign or_1_out = shifter_1_out | bit_extender_1_out;  // OR_Gate or_1, 12 bits wide
  // Probe on register_1_q
  Register #(.width(12)) register_1 (.D(or_1_out), .Q(register_1_q), .clk(clk), .clr(reset));  // open: en
  Multiplexer #(.width(2)) multiplexer_2 (
    .in0(2'b00), .in1(2'b10), .out(multiplexer_2_out), .sel(comparator_1_eq));  // open: en
  Comparator #(.width(12), .mode("unsigned")) comparator_1 (
    .a(12'h82f), .b(or_1_out), .eq(comparator_1_eq));  // open: gt, lt
  Comparator #(.width(12), .mode("unsigned")) comparator_2 (
    .a(12'h244), .b(or_1_out), .eq(comparator_2_eq));  // open: gt, lt
  Multiplexer #(.width(2)) multiplexer_3 (
    .in0(multiplexer_2_out), .in1(2'b01), .out(\output ), .sel(comparator_2_eq));  // open: en
endmodule
