// Logisim project P0_L1_score.circ as structural Verilog
module score (
  input  [2:0] tea,
  input  [1:0] s1,
  input  [1:0] s2,
  output [3:0] out_4
);

  wire comparator_1_eq;
  wire [3:0] adder_1_out, adder_2_out, bit_extender_1_out, bit_extender_2_out, bit_extender_3_out;

  assign bit_extender_1_out = {{1{1'b0}}, tea};  // Bit_Extender bit_extender_1
  assign bit_extender_2_out = {{2{1'b0}}, s1};  // Bit_Extender bit_extender_2
  assign bit_extender_3_out = {{2{1'b0}}, s2};  // Bit_Extender bit_extender_3
  Adder #(.width(4)) adder_1 (.a(bit_extender_2_out), .b(bit_extender_3_out), .out(adder_1_out));  // open: cin, cout
  Adder #(.width(4)) adder_2 (.a(bit_extender_1_out), .b(adder_1_out), .out(adder_2_out));  // open: cin, cout
  Multiplexer #(.width(4)) multiplexer_1 (
    .in0(adder_2_out), .in1(4'b0000), .out(out_4), .sel(comparator_1_eq));  // open: en
  Comparator #(.width(4), .mode("unsigned")) comparator_1 (
    .a(bit_extender_1_out), .b(4'b0000), .eq(comparator_1_eq));  // open: gt, lt
endmodule
