// Logisim project P0_L1_series_2023.circ as structural Verilog: 1 circuit, main circuit main
module main (
  input  [1:0] \type ,
  input  reset,
  input  clk,
  output [31:0] out_4
);

  wire [31:0] adder_1_out, adder_2_out, multiplexer_1_out, multiplexer_2_out, multiplexer_3_out, sum_n_q;

  Adder #(.width(32)) adder_1 (.a(out_4), .b(32'h1), .out(adder_1_out));  // open: cin, cout
  Adder #(.width(32)) adder_2 (.a(out_4), .b(sum_n_q), .out(adder_2_out));  // open: cin, cout
  Multiplexer #(.select(2), .width(32)) multiplexer_1 (
    .in0({32{1'b0}}), .in1(adder_1_out), .in2(adder_2_out), .out(multiplexer_1_out), .sel(\type ));  // open: in3, en
  Multiplexer #(.width(32)) multiplexer_2 (
    .in0(adder_2_out), .in1({32{1'b0}}), .out(multiplexer_2_out), .sel(reset));  // open: en
  Multiplexer #(.width(32)) multiplexer_3 (
    .in0(multiplexer_1_out), .in1({32{1'b0}}), .out(multiplexer_3_out), .sel(reset));  // open: en
  Register #(.width(32)) sum_n (.D(multiplexer_2_out), .Q(sum_n_q), .clk(clk));  // open: en, clr
  Register #(.width(32)) a_n (.D(multiplexer_3_out), .Q(out_4), .clk(clk));  // open: en, clr
endmodule
