// Logisim project P0_L4_interview.circ as structural Verilog
module interview (
  input  [2:0] standar,
  input  [2:0] tea,
  input  [1:0] s1,
  input  [1:0] s2,
  output outcome
);

  wire comparator_1_eq, comparator_2_lt, multiplexer_1_out;
  wire [31:0] adder_1_out, adder_2_out, bit_extender_1_out, bit_extender_2_out, bit_extender_3_out,
       bit_extender_4_out;

  assign bit_extender_1_out = {{29{1'b0}}, standar};  // Bit_Extender bit_extender_1
  assign bit_extender_2_out = {{29{1'b0}}, tea};  // Bit_Extender bit_extender_2
  assign bit_extender_3_out = {{30{1'b0}}, s1};  // Bit_Extender bit_extender_3
  assign bit_extender_4_out = {{30{1'b0}}, s2};  // Bit_Extender bit_extender_4
  Adder #(.width(32)) adder_1 (.a(bit_extender_3_out), .b(bit_extender_4_out), .out(adder_1_out));  // open: cin, cout
  Comparator #(.width(3), .mode("unsigned")) comparator_1 (.a(tea), .b(3'b000), .eq(comparator_1_eq));  // open: gt, lt
  Adder #(.width(32)) adder_2 (.a(bit_extender_2_out), .b(adder_1_out), .out(adder_2_out));  // open: cin, cout
  Multiplexer multiplexer_1 (.in0(1'b0), .in1(1'b1), .out(multiplexer_1_out), .sel(comparator_2_lt));  // open: en
  Comparator #(.width(32), .mode("unsigned")) comparator_2 (
    .a(bit_extender_1_out), .b(adder_2_out), .lt(comparator_2_lt));  // open: gt, eq
  Multiplexer multiplexer_2 (.in0(multiplexer_1_out), .in1(1'b0), .out(outcome), .sel(comparator_1_eq));  // open: en
endmodule
