// Logisim project P0_L6_multiply_2023.circ as structural Verilog: 1 circuit, main circuit main
module main (
  input  [7:0] input1,
  input  [7:0] input2,
  input  reset,
  input  clk,
  output [7:0] out_5
);

  wire comparator_1_eq;
  wire [3:0] bitadder_1_out, bitadder_2_out;
  wire [7:0] a_n_1, adder_1_out, adder_2_out, bit_extender_1_out, bit_extender_2_out, multiplexer_1_out,
       multiplexer_2_out, multiplexer_3_out, multiplexer_4_out, multiplier_1_out, or_1_out;

  BitAdder bitadder_1 (.in0(a_n_1), .out(bitadder_1_out));
  BitAdder bitadder_2 (.in0(out_5), .out(bitadder_2_out));
  assign bit_extender_1_out = {{4{1'b0}}, bitadder_1_out};  // Bit_Extender bit_extender_1
  assign bit_extender_2_out = {{4{1'b0}}, bitadder_2_out};  // Bit_Extender bit_extender_2
  assign or_1_out = input1 | input2;  // OR_Gate or_1, 8 bits wide
  Adder adder_1 (.a(bit_extender_1_out), .b(8'h3), .out(adder_1_out));  // open: cin, cout
  Adder adder_2 (.a(bit_extender_2_out), .b(8'h1), .out(adder_2_out));  // open: cin, cout
  Comparator #(.mode("unsigned")) comparator_1 (.a(or_1_out), .b({8{1'b0}}), .eq(comparator_1_eq));  // open: gt, lt
  Multiplexer #(.width(8)) multiplexer_1 (
    .in0(input1), .in1(out_5), .out(multiplexer_1_out), .sel(comparator_1_eq));  // open: en
  Multiplexer #(.width(8)) multiplexer_2 (
    .in0(input2), .in1(multiplier_1_out), .out(multiplexer_2_out), .sel(comparator_1_eq));  // open: en
  Multiplier multiplier_1 (.a(adder_1_out), .b(adder_2_out), .out(multiplier_1_out));  // open: cin, cout
  Multiplexer #(.width(8)) multiplexer_3 (
    .in0(multiplexer_1_out), .in1({8{1'b0}}), .out(multiplexer_3_out), .sel(reset));  // open: en
  Multiplexer #(.width(8)) multiplexer_4 (
    .in0(multiplexer_2_out), .in1({8{1'b0}}), .out(multiplexer_4_out), .sel(reset));  // open: en
  Register a0 (.D(multiplexer_3_out), .Q(a_n_1), .clk(clk));  // open: en, clr
  Register a1 (.D(multiplexer_4_out), .Q(out_5), .clk(clk));  // open: en, clr

  // Other names for the same wires on the sheet: a_n[7:0] = out_5
endmodule
