// Logisim project P3_L0_Weak.circ as structural Verilog: 9 circuits, main circuit main
module main (
  input  Reset,
  output [31:0] Instr,
  output [31:0] PC,
  output RegWrite,
  output [4:0] RegAddr,
  output [31:0] RegData,
  output MemWrite,
  output [31:0] MemAddr,
  output [31:0] MemData
);

  wire ALUSrc, Clk, ctrl_1_dmsel, eq;
  wire [1:0] ALUOp, EXTOp, NPCOp, RegDst, RegSrc;
  wire [4:0] Rd, Rs, Rt;
  wire [5:0] mysplitter_1_funct, mysplitter_1_op;
  wire [15:0] Imm;
  wire [31:0] dm_1_memrd, Extend_Imm, grf_1_rd1, multiplexer_3_out, npc_1_npc;

  Clock clock_1 (.out(Clk));
  Multiplexer #(.select(2), .width(5)) multiplexer_1 (
    .in0(Rt), .in1(Rd), .out(RegAddr), .sel(RegDst));  // open: in2, in3, en
  Multiplexer #(.select(2), .width(32)) multiplexer_2 (
    .in0(MemAddr), .in1(dm_1_memrd), .in2(Extend_Imm), .out(RegData), .sel(RegSrc));  // open: in3, en
  IFU ifu_1 (.NextPC(npc_1_npc), .reset(Reset), .Instr(Instr), .PC(PC), .clk(Clk));
  NPC npc_1 (.NPC(npc_1_npc), .PC(PC), .Extend_Imm(Extend_Imm), .NPCOp(NPCOp), .in_6(eq));  // open: Imm26, reg, out_8
  // Probe on Instr
  GRF grf_1 (
    .A1(Rs), .A2(Rt), .A3(RegAddr), .WD(RegData), .RD1(grf_1_rd1), .RD2(MemData), .clk(Clk), .reset(Reset),
    .WE(RegWrite));
  EXT ext_1 (.Imm(Imm), .EXTOp(EXTOp), .extened_Imm(Extend_Imm));
  MySplitter mysplitter_1 (
    .Instr(Instr), .OP(mysplitter_1_op), .Rs(Rs), .Rt(Rt), .Rd(Rd), .Funct(mysplitter_1_funct), .Imm(Imm));  // open: J_addr, Shamt
  Multiplexer #(.width(32)) multiplexer_3 (
    .in0(MemData), .in1(Extend_Imm), .out(multiplexer_3_out), .sel(ALUSrc));  // open: en
  ALU alu_1 (.A(grf_1_rd1), .A_2(multiplexer_3_out), .res(MemAddr), .eq(eq), .ALUOp(ALUOp));
  Ctrl ctrl_1 (
    .Funct(mysplitter_1_funct), .Op(mysplitter_1_op), .RegDst(RegDst), .RegWrite(RegWrite),
    .MemWrite(MemWrite), .EXTOp(EXTOp), .ALUSrc(ALUSrc), .ALUOp(ALUOp), .NPCOp(NPCOp), .RegSrc(RegSrc),
    .DMSel(ctrl_1_dmsel));
  DM dm_1 (
    .MemAddr(MemAddr), .MemData(MemData), .MemRD(dm_1_memrd), .in_3(MemWrite), .in_4(Clk), .in_5(1'b1),
    .in_6(Reset), .DMSel(ctrl_1_dmsel));

  // Other names for the same wires on the sheet: res[31:0] = MemAddr
endmodule

module GRF (
  input  clk,
  input  reset,
  input  WE,
  input  [4:0] A1,
  input  [4:0] A2,
  input  [4:0] A3,
  input  [31:0] WD,
  output [31:0] RD1,
  output [31:0] RD2
);

  wire [31:0] in1, in2, in3, in4, in5, in6, in7, in8, in9, in10, in11, in12, in13, in14, in15, in16, in17,
       in18, in19, in20, in21, in22, in23, in24, in25, in26, in27, in28, in29, in30, in31, out0, out1, out2,
       out3, out4, out5, out6, out7, out8, out9, out10, out11, out12, out13, out14, out15, out16, out17,
       out18, out19, out20, out21, out22, out23, out24, out25, out26, out27, out28, out29, out30, out31;

  // Probe on in2
  // Probe on out24
  // Probe on in24
  // Probe on in2
  Demultiplexer #(.select(5), .width(32), .tristate("true")) demultiplexer_1 (
    .out1(in1), .out2(in2), .out3(in3), .out4(in4), .out5(in5), .out6(in6), .out7(in7), .out8(in8),
    .out9(in9), .out10(in10), .out11(in11), .out12(in12), .out13(in13), .out14(in14), .out15(in15),
    .out16(in16), .out17(in17), .out18(in18), .out19(in19), .out20(in20), .out21(in21), .out22(in22),
    .out23(in23), .out24(in24), .out25(in25), .out26(in26), .out27(in27), .out28(in28), .out29(in29),
    .out30(in30), .out31(in31), .in(WD), .sel(A3));  // open: out0, en
  Register #(.width(32)) \_0_只读_为0_不可写  (.en(WE), .Q(out0), .clk(clk), .clr(reset));  // open: D
  Register #(.width(32)) _4 (.D(in4), .en(WE), .Q(out4), .clk(clk), .clr(reset));
  Register #(.width(32)) _8 (.D(in8), .en(WE), .Q(out8), .clk(clk), .clr(reset));
  Register #(.width(32)) _12 (.D(in12), .en(WE), .Q(out12), .clk(clk), .clr(reset));
  Register #(.width(32)) _16 (.D(in16), .en(WE), .Q(out16), .clk(clk), .clr(reset));
  Register #(.width(32)) _20 (.D(in20), .en(WE), .Q(out20), .clk(clk), .clr(reset));
  Register #(.width(32)) _24 (.D(in24), .en(WE), .Q(out24), .clk(clk), .clr(reset));
  Register #(.width(32)) _28 (.D(in28), .en(WE), .Q(out28), .clk(clk), .clr(reset));
  Register #(.width(32)) _1 (.D(in1), .en(WE), .Q(out1), .clk(clk), .clr(reset));
  Register #(.width(32)) _5 (.D(in5), .en(WE), .Q(out5), .clk(clk), .clr(reset));
  Register #(.width(32)) _9 (.D(in9), .en(WE), .Q(out9), .clk(clk), .clr(reset));
  Register #(.width(32)) _13 (.D(in13), .en(WE), .Q(out13), .clk(clk), .clr(reset));
  Register #(.width(32)) _17 (.D(in17), .en(WE), .Q(out17), .clk(clk), .clr(reset));
  Register #(.width(32)) _21 (.D(in21), .en(WE), .Q(out21), .clk(clk), .clr(reset));
  Register #(.width(32)) _25 (.D(in25), .en(WE), .Q(out25), .clk(clk), .clr(reset));
  Register #(.width(32)) _29 (.D(in29), .en(WE), .Q(out29), .clk(clk), .clr(reset));
  Register #(.width(32)) _2 (.D(in2), .en(WE), .Q(out2), .clk(clk), .clr(reset));
  Register #(.width(32)) _6 (.D(in6), .en(WE), .Q(out6), .clk(clk), .clr(reset));
  Register #(.width(32)) _10 (.D(in10), .en(WE), .Q(out10), .clk(clk), .clr(reset));
  Register #(.width(32)) _14 (.D(in14), .en(WE), .Q(out14), .clk(clk), .clr(reset));
  Register #(.width(32)) _18 (.D(in18), .en(WE), .Q(out18), .clk(clk), .clr(reset));
  Register #(.width(32)) _22 (.D(in22), .en(WE), .Q(out22), .clk(clk), .clr(reset));
  Register #(.width(32)) _26 (.D(in26), .en(WE), .Q(out26), .clk(clk), .clr(reset));
  Register #(.width(32)) _30 (.D(in30), .en(WE), .Q(out30), .clk(clk), .clr(reset));
  Register #(.width(32)) _3 (.D(in3), .en(WE), .Q(out3), .clk(clk), .clr(reset));
  Register #(.width(32)) _7 (.D(in7), .en(WE), .Q(out7), .clk(clk), .clr(reset));
  Register #(.width(32)) _11 (.D(in11), .en(WE), .Q(out11), .clk(clk), .clr(reset));
  Register #(.width(32)) _15 (.D(in15), .en(WE), .Q(out15), .clk(clk), .clr(reset));
  Register #(.width(32)) _19 (.D(in19), .en(WE), .Q(out19), .clk(clk), .clr(reset));
  Register #(.width(32)) _23 (.D(in23), .en(WE), .Q(out23), .clk(clk), .clr(reset));
  Register #(.width(32)) _27 (.D(in27), .en(WE), .Q(out27), .clk(clk), .clr(reset));
  Register #(.width(32)) _31 (.D(in31), .en(WE), .Q(out31), .clk(clk), .clr(reset));
  Multiplexer #(.select(5), .width(32)) multiplexer_1 (
    .in0(out0), .in1(out1), .in2(out2), .in3(out3), .in4(out4), .in5(out5), .in6(out6), .in7(out7),
    .in8(out8), .in9(out9), .in10(out10), .in11(out11), .in12(out12), .in13(out13), .in14(out14),
    .in15(out15), .in16(out16), .in17(out17), .in18(out18), .in19(out19), .in20(out20), .in21(out21),
    .in22(out22), .in23(out23), .in24(out24), .in25(out25), .in26(out26), .in27(out27), .in28(out28),
    .in29(out29), .in30(out30), .in31(out31), .out(RD1), .sel(A1));  // open: en
  Multiplexer #(.select(5), .width(32)) multiplexer_2 (
    .in0(out0), .in1(out1), .in2(out2), .in3(out3), .in4(out4), .in5(out5), .in6(out6), .in7(out7),
    .in8(out8), .in9(out9), .in10(out10), .in11(out11), .in12(out12), .in13(out13), .in14(out14),
    .in15(out15), .in16(out16), .in17(out17), .in18(out18), .in19(out19), .in20(out20), .in21(out21),
    .in22(out22), .in23(out23), .in24(out24), .in25(out25), .in26(out26), .in27(out27), .in28(out28),
    .in29(out29), .in30(out30), .in31(out31), .out(RD2), .sel(A2));  // open: en
endmodule

module IFU (
  input  [31:0] NextPC,
  input  reset,
  input  clk,
  output [31:0] Instr,
  output [31:0] PC
);

  wire counter_1_q;
  wire [31:0] PC_q, subtractor_1_out;

  Register #(.width(32)) u_PC (.D(NextPC), .Q(PC_q), .clk(clk), .clr(reset));  // open: en
  Multiplexer #(.width(32)) multiplexer_1 (.in0(32'h3000), .in1(PC_q), .out(PC), .sel(counter_1_q));  // open: en
  Counter #(.width(1), .max('h1), .ongoal("stay")) counter_1 (
    .Q(counter_1_q), .clk(clk), .clr(reset));  // open: load, D, count, carry
  // Probe on subtractor_1_out[13:2]
  Subtractor #(.width(32)) subtractor_1 (.a(PC), .b(32'h3000), .out(subtractor_1_out));  // open: bin, bout
  // Probe on subtractor_1_out
  ROM #(.addrWidth(12), .dataWidth(32)) rom_1 (.addr(subtractor_1_out[13:2]), .data(Instr));  // open: sel

  // Notes on the sheet:
  //   IM
  //   contents of rom_1 (hex, n*v repeats v):
  //   3401003c ac2cffd0 3401003c ac32ffec 3401003c ac23ffcc 3401003c 8c300000 ac010038 ac0f001c 14ea020
  //   ac0e0018 8c140030 144c820 3401003c 8c3cfff8 3401003c ac33fff8 3c13ca90 8c020038 8c1d001c 27fc820
  //   3401003c ac2affd8 341e020 3401003c 8c21ffd8 3c1d2d4d 2418022 3401003c ac35ffe4 3401003c 8c2affd4
  //   3401003c ac34ffd4 3401003c 8c2cffe4 ac10003c ac16000c 311820 38f5022 8c190024 3401003c ac2fffcc
  //   3401003c 8c360004 8c0c000c 3401003c ac34ffd8 3401003c ac2efff0 3401003c ac28ffcc 1aad022 3c0f06e7
  //   8c16000c 3c09cfd4 3401003c 8c2a0020 3c1e3608 3401003c ac2effd4 3401003c ac38ffc4 8c160030 ac1f0010
  //   3c1d22c7 3df5820 8c110008 2e1c022 ac06003c 3401003c ac2dffdc 3401003c ac3a0004 3401003c ac38ffe8
  //   30c7820 3401003c 8c29ffd8 3401003c 8c3cffec 3401003c 8c33ffe4 3401003c ac3affd0 3401003c ac390000
  //   3401003c ac24ffc8 8c090030 3401003c ac3cffd8 3401003c ac310000 3401003c ac230000 33c2022 ac010010
  //   3401003c 8c2effec 3401003c ac25fff8 3401003c ac27ffe8 3c0560eb 3401003c 8c24ffc8 3401003c 8c29ffec
  //   ac1f0004 384e822 3401003c ac3bffcc 3c026a96 3401003c 8c2fffe8 3401003c ac390020 ac1a000c 8c170004
  //   3401003c 8c3bffd4 8c090028 3401003c ac27fff8 1932022 2b1f022 8c1e0020 3401003c ac35ffd4 8c030010
  //   2cb9822 3401003c ac25ffec 3401003c ac35ffec 8c060000 8c150018 8c020024 3401003c ac27ffcc ac1b000c
  //   3401003c ac2dffcc ac120010 3401003c ac350020 3401003c 8c23fff4 ac0b0004 ac020004 3401003c 8c21ffdc
  //   315a022 3401003c 8c30ffd8 3fde820 8c120008 ed5022 3401003c ac29fff8 ac14001c 3401003c ac36ffd0
  //   3401003c ac38ffe4 11aa020 ac1e0004 ac11000c 3c1d90b6 3401003c ac28ffe8 3401003c ac37ffd8 3c1eccb5
  //   3c0b5190 3401003c ac28ffec 3f4a022 3401003c ac3cffd0 3401003c 8c28ffd4 1a9d822 3c105e99 3c0af13e
  //   47b022 8c060020 3401003c ac31ffd8 2c5820 3401003c ac37ffd0 3401003c ac310004 3c07ee5d ac020038
  //   8c160030 8c1b003c ac080028 ac1d0020 3401003c ac35ffd0 3401003c ac3a0000 3401003c ac23ffd0 3401003c
  //   ac23fff8 3c18575d 8c1e0034 3401003c 8c3ffff8 478022 3401003c ac26fff8 3c1f9382 1713020 3401003c
  //   8c3bffd0 3401003c 8c260000 8c16000c 68f822 3da8022 3f05022 3401003c ac22fff8 3401003c ac240000
  //   3c0b6ec5 df5020 3401003c ac3b0004 3401003c 8c36ffd4 3401003c ac35ffdc 3c10d6ed 8c17001c 633020
  //   ac0e0004 3401003c ac3bfff4 37b5020 3401003c ac290004 8c180030 3401003c ac2dffc4 456820 3401003c
  //   ac38ffc4 3401003c ac2dffcc 3401003c 8c2effc4 3401003c ac3dffc8 3401003c 8c30ffe4 ac1e0018 3401003c
  //   ac340000 8c1f0038 3401003c ac230020 8c0e000c 3c09f48e 38f4020 3401003c ac3fffcc ac0c0000 8c050020
  //   3c038c4a 3401003c ac270004 3401003c ac2affc8 23c2822 8c1e0000 3401003c ac36ffec 3401003c ac26fff0
  //   292b020 269c822 3c07efac ac0d000c 3401003c ac23fff8 ac17000c 8c060010 3401003c ac3d0020 3401003c
  //   ac320000 3401003c ac3bfff4 3bb8820 3401003c ac29ffd8 8c190014 ac0b002c 2136020 3401003c ac37ffcc
  //   141e820 8c160028 3401003c ac29ffec 3401003c ac36ffd4 3c01e41c 3401003c ac33ffdc 3c0e6ca7 3401003c
  //   ac2fffcc 2a71822 3401003c 8c3fffd4 3401003c ac31ffe4 3401003c ac33ffcc 3401003c ac2bffe4 3401003c
  //   ac21ffe8 3401003c ac2ffff4 3401003c ac28ffd4 3401003c ac2affec ac140028 3401003c ac3dfff8 3401003c
  //   ac34ffd0 3401003c ac21ffe4 3401003c ac27fff0 3401003c ac22ffd0 ac080008 8c0a0038 ac150030 3401003c
  //   ac2bffd8 8c080020 2952020 8c1f0010 3401003c ac2cffc8 3401003c ac22fff8 13d4820 3401003c ac2affdc
  //   3401003c ac2dffcc ac090034 3401003c ac250004 3c177d21 3401003c 8c25ffc8 3401003c ac310000 3401003c
  //   ac2cffc8 3c089006 35ad822 3401003c 8c25fff8 3401003c ac2effe8 3401003c ac37ffd0 3401003c 8c23ffd0
  //   ac11000c 3071022 3401003c 8c3fffdc 3401003c ac30fff8 8c0e000c 3fe3820 3c10bc5f 3401003c ac2efff0
  //   3401003c ac31ffe8 3b6e820 3401003c 8c2afff0 3c0a0450 ac190038 8c14000c ac1d000c 3401003c ac22fff0
  //   ac120028 3c02f370 8c1b0010 3401003c 8c380000 837820 8c030014 521020 3401003c ac25ffdc 3c045ce3
  //   8c0d001c 1046822 3c0d706d 3401003c ac380020 3401003c ac27ffc4 ac070038 116d820 3401003c ac26ffec
  //   3c0a9374 30f2020 165c820 3401003c ac28fff8 8c030010 3401003c ac35ffec 3401003c ac2cffdc 2c1b822
  //   3401003c ac2effcc 290a020 8c110004 156f020 8c100014 3401003c ac26ffd4 3401003c ac29ffdc 3401003c
  //   ac22ffe8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
endmodule

module MySplitter (
  input  [31:0] Instr,
  output [5:0] OP,
  output [4:0] Rs,
  output [4:0] Rt,
  output [4:0] Rd,
  output [5:0] Funct,
  output [15:0] Imm,
  output [25:0] J_addr,
  output [4:0] Shamt
);


  assign Funct = Instr[5:0];
  assign Imm = Instr[15:0];
  assign J_addr = Instr[25:0];
  assign OP = Instr[31:26];
  assign Rd = Instr[15:11];
  assign Rs = Instr[25:21];
  assign Rt = Instr[20:16];
  assign Shamt = Instr[10:6];
endmodule

module EXT (
  input  [15:0] Imm,
  input  [1:0] EXTOp,
  output [31:0] extened_Imm
);

  wire [31:0] bit_extender_1_out, bit_extender_2_out, bit_extender_3_out, shifter_1_out;

  assign bit_extender_1_out = {{16{1'b0}}, Imm};  // Bit_Extender bit_extender_1
  assign bit_extender_2_out = {{16{Imm[15]}}, Imm};  // Bit_Extender bit_extender_2
  assign bit_extender_3_out = {{16{1'b0}}, Imm};  // Bit_Extender bit_extender_3
  Shifter #(.width(32)) shifter_1 (.in(bit_extender_3_out), .\dist (5'b10000), .out(shifter_1_out));
  Multiplexer #(.select(2), .width(32)) multiplexer_1 (
    .in0(bit_extender_1_out), .in1(bit_extender_2_out), .in2(shifter_1_out), .out(extened_Imm), .sel(EXTOp));  // open: in3, en
endmodule

module NPC (
  input  [31:0] PC,
  input  [31:0] Extend_Imm,
  input  [25:0] Imm26,
  input  [31:0] \reg ,
  input  [1:0] NPCOp,
  input  in_6,
  output [31:0] NPC,
  output [31:0] out_8
);

  wire [31:0] adder_2_out, multiplexer_2_out, shifter_1_out;

  Multiplexer #(.select(2), .width(32)) multiplexer_1 (
    .in0(out_8), .in1(multiplexer_2_out), .out(NPC), .sel(NPCOp));  // open: in2, in3, en
  Multiplexer #(.width(32)) multiplexer_2 (
    .in0(out_8), .in1(adder_2_out), .out(multiplexer_2_out), .sel(in_6));  // open: en
  Adder #(.width(32)) adder_1 (.a(PC), .b(32'h4), .out(out_8));  // open: cin, cout
  Shifter #(.width(32)) shifter_1 (.in(Extend_Imm), .\dist (5'b00010), .out(shifter_1_out));
  Adder #(.width(32)) adder_2 (.a(out_8), .b(shifter_1_out), .out(adder_2_out));  // open: cin, cout

  // Other names for the same wires on the sheet: eq = in_6; PC_4[31:0] = out_8

  // Notes on the sheet:
  //   1、顺序更新
  //   2、b跳转类型
  //   3、j跳转类型
  //   4、jr跳转类型
  //   jr、jalr
  //   j、jal
endmodule

module ALU (
  input  [31:0] A,
  input  [31:0] A_2,
  input  [1:0] ALUOp,
  output [31:0] res,
  output eq
);

  wire [31:0] adder_1_out, or_1_out, subtractor_1_out;

  Adder #(.width(32)) adder_1 (.a(A), .b(A_2), .out(adder_1_out));  // open: cin, cout
  Subtractor #(.width(32)) subtractor_1 (.a(A), .b(A_2), .out(subtractor_1_out));  // open: bin, bout
  assign or_1_out = A | A_2;  // OR_Gate or_1, 32 bits wide
  Comparator #(.width(32), .mode("unsigned")) comparator_1 (.a(A), .b(A_2), .eq(eq));  // open: gt, lt
  Multiplexer #(.select(2), .width(32)) multiplexer_1 (
    .in0(adder_1_out), .in1(subtractor_1_out), .in2(or_1_out), .out(res), .sel(ALUOp));  // open: in3, en
endmodule

// DMSel
module Ctrl (
  input  [5:0] Funct,
  input  [5:0] Op,
  output [1:0] EXTOp,
  output [1:0] ALUOp,
  output [1:0] RegSrc,
  output DMSel,
  output [1:0] NPCOp,
  output [1:0] RegDst,
  output RegWrite,
  output MemWrite,
  output ALUSrc
);

  wire add_out, and_1_out, and_2_out, and_3_out, beq_out, lui_out, lw_out, not_1_out, not_2_out, not_3_out,
       not_4_out, not_5_out, not_6_out, not_7_out, not_8_out, not_9_out, not_10_out, not_11_out, not_12_out,
       ori_out, R_Instr_out, sub_out, sw_out;

  not not_1 (not_1_out, Op[5]);
  not not_2 (not_2_out, Op[4]);
  not not_3 (not_3_out, Op[3]);
  not not_4 (not_4_out, Op[1]);
  not not_5 (not_5_out, Op[2]);
  not not_6 (not_6_out, Op[0]);
  and R_Instr (R_Instr_out, not_6_out, not_4_out, not_5_out, not_3_out, not_2_out, not_1_out);
  not not_7 (not_7_out, Funct[5]);
  not not_8 (not_8_out, Funct[4]);
  not not_9 (not_9_out, Funct[3]);
  not not_10 (not_10_out, Funct[2]);
  not not_11 (not_11_out, Funct[1]);
  not not_12 (not_12_out, Funct[0]);
  and and_1 (and_1_out, not_12_out, not_11_out, not_10_out, not_9_out, not_8_out, Funct[5]);
  and and_2 (and_2_out, not_12_out, Funct[1], not_10_out, not_9_out, not_8_out, Funct[5]);
  and add (add_out, and_1_out, R_Instr_out);
  and sub (sub_out, and_2_out, R_Instr_out);
  and ori (ori_out, Op[0], not_4_out, Op[2], Op[3], not_2_out, not_1_out);
  and lui (lui_out, Op[0], Op[1], Op[2], Op[3], not_2_out, not_1_out);
  and beq (beq_out, not_6_out, not_4_out, Op[2], not_3_out, not_2_out, not_1_out);
  and lw (lw_out, Op[0], Op[1], not_5_out, not_3_out, not_2_out, Op[5]);
  and sw (sw_out, Op[0], Op[1], not_5_out, Op[3], not_2_out, Op[5]);
  // AND_Gate and_3 has open pins: out=and_3_out
  or bit0 (RegDst[0], add_out, sub_out);
  buf or_1 (RegSrc[1], lui_out);  // OR_Gate
  buf or_2 (RegSrc[0], lw_out);  // OR_Gate
  or or_3 (RegWrite, add_out, sub_out, ori_out, lui_out, lw_out);
  buf or_4 (MemWrite, sw_out);  // OR_Gate
  buf bit1 (EXTOp[1], lui_out);  // OR_Gate
  or bit0_2 (EXTOp[0], beq_out, lw_out, sw_out);
  or or_5 (ALUSrc, ori_out, lw_out, sw_out);
  buf bit1_2 (ALUOp[1], ori_out);  // OR_Gate
  buf bit0_3 (ALUOp[0], sub_out);  // OR_Gate
  buf bit0_4 (NPCOp[0], beq_out);  // OR_Gate
  // OR_Gate or_6 is placed but not wired

  assign DMSel = 1'b0;
  assign NPCOp[1] = 1'b0;
  assign RegDst[1] = 1'b0;

  // Notes on the sheet:
  //   add new instruction here!
endmodule

module DM (
  input  DMSel,
  input  [31:0] MemAddr,
  input  in_3,
  input  in_4,
  input  in_5,
  input  in_6,
  input  [31:0] MemData,
  output [31:0] MemRD
);

  wire decoder_1_out0, decoder_1_out1, decoder_1_out2, decoder_1_out3;
  wire [7:0] multiplexer_2_out;
  wire [31:0] bit_extender_1_out, multiplexer_1_out, multiplexer_3_out, ram_1_data;

  Multiplexer #(.width(32)) multiplexer_1 (
    .in0(MemData), .in1(multiplexer_3_out), .out(multiplexer_1_out), .sel(DMSel));  // open: en
  Decoder #(.select(2)) decoder_1 (
    .out0(decoder_1_out0), .out1(decoder_1_out1), .out2(decoder_1_out2), .out3(decoder_1_out3),
    .sel(MemAddr[1:0]));  // open: en
  RAM #(.addrWidth(12), .dataWidth(32), .bus("separate")) ram_1 (
    .addr(MemAddr[13:2]), .din(multiplexer_1_out), .data(ram_1_data), .str(in_3), .clk(in_4), .ld(in_5),
    .clr(in_6));  // open: sel
  Multiplexer #(.select(2), .width(8)) multiplexer_2 (
    .in0(ram_1_data[7:0]), .in1(ram_1_data[15:8]), .in2(ram_1_data[23:16]), .in3(ram_1_data[31:24]),
    .out(multiplexer_2_out), .sel(MemAddr[1:0]));  // open: en
  Multiplexer #(.width(8)) multiplexer_3 (
    .in0(ram_1_data[7:0]), .in1(MemData[7:0]), .out(multiplexer_3_out[7:0]), .sel(decoder_1_out0));  // open: en
  Multiplexer #(.width(8)) multiplexer_4 (
    .in0(ram_1_data[15:8]), .in1(MemData[7:0]), .out(multiplexer_3_out[15:8]), .sel(decoder_1_out1));  // open: en
  Multiplexer #(.width(8)) multiplexer_5 (
    .in0(ram_1_data[23:16]), .in1(MemData[7:0]), .out(multiplexer_3_out[23:16]), .sel(decoder_1_out2));  // open: en
  Multiplexer #(.width(8)) multiplexer_6 (
    .in0(ram_1_data[31:24]), .in1(MemData[7:0]), .out(multiplexer_3_out[31:24]), .sel(decoder_1_out3));  // open: en
  assign bit_extender_1_out = {{24{multiplexer_2_out[7]}}, multiplexer_2_out};  // Bit_Extender bit_extender_1
  Multiplexer #(.width(32)) multiplexer_7 (
    .in0(ram_1_data), .in1(bit_extender_1_out), .out(MemRD), .sel(DMSel));  // open: en

  // Other names for the same wires on the sheet: Addr_1_0[1:0] = MemAddr[1:0]
endmodule
